// Logisim project cpu.circ as structural Verilog: 16 circuits, main circuit Controller
module cpu (
);

  wire and_1_out, CLK, CTL, Fail, lock_IF_ID, lock_PC, or_1_out, or_2_out, RST, rst_ID_EX, syscall_res_n;
  wire [2:0] controller_1_pc_control, id_ex_1_out_24;
  wire [4:0] controller_1_instruction, controller_1_ra, controller_1_rb, decoder_1_shamt, ex_mem_1_out_11,
       id_ex_1_out_16, mem_wb_1_out_10;
  wire [5:0] controller_1_mem, decoder_1_funct, decoder_1_op, ex_mem_1_out_13, id_ex_1_out_18;
  wire [6:0] controller_1_ex, id_ex_1_out_19;
  wire [7:0] controller_1_wb, ex_mem_1_out_12, id_ex_1_out_17, registerfile_1_p4;
  wire [9:0] divider_1_out_2;
  wire [11:0] controller_1_will_r;
  wire [14:0] decoder_1_mix;
  wire [15:0] decoder_1_imm, \总周期数 , \无条件分支指令数 , \有条件分支成功跳转 , \有条件分支指令数 ;
  wire [23:0] divider1_1_out_2;
  wire [25:0] decoder_1_label, id_ex_1_out_25;
  wire [31:0] alu_1_result, ex_mem_1_out_10, ex_mem_1_out_14, ex_mem_1_out_15, extender_1_out_3,
       extender_1_out_4, id_ex_1_out_15, id_ex_1_out_20, id_ex_1_out_21, id_ex_1_out_22, id_ex_1_out_23,
       if_id_1_out_6, if_id_1_out_7, mem_wb_1_out_9, mem_wb_1_out_12, mem_wb_1_out_13, mips_ram_1_p8,
       multiplexer_1_out, multiplexer_2_out, multiplexer_3_out, npc_1_new_pc, npc_1_pc4, PC_q,
       registerfile_1_p7, registerfile_1_p8, rom_1_data, SyscallOut;

  Clock clock_1 (.out(CLK));
  Button \u_总复位  (.out(RST));
  Register #(.width(32)) PC (.D(npc_1_new_pc), .en(and_1_out), .Q(PC_q), .clk(CLK), .clr(RST));
  and and_1 (and_1_out, CTL, lock_PC);
  SumPeriod sumperiod_1 (.in_1(CTL), .in_2(CLK), .out_4(\总周期数 ), .in_3(RST));
  NPC npc_1 (
    .PC_input(PC_q), .new_PC(npc_1_new_pc), .label(id_ex_1_out_25), .IMM(id_ex_1_out_23),
    .RF1(id_ex_1_out_20), .pc_control(id_ex_1_out_24), .PC4(npc_1_pc4), .RF2(id_ex_1_out_21), .rst(RST),
    .clk(CLK), .\成功Cnt (\有条件分支成功跳转 ), .syscall(syscall_res_n), .en(CTL), .oldPC(id_ex_1_out_15),
    .ALUout(alu_1_result), .fail(Fail));
  Hex_Digit_Display hex_digit_display_1 (.value(SyscallOut[31:28]));  // open: dp
  Hex_Digit_Display hex_digit_display_2 (.value(SyscallOut[27:24]));  // open: dp
  Divider divider_1 (.in_1(PC_q), .out_2(divider_1_out_2));
  Hex_Digit_Display hex_digit_display_3 (.value(SyscallOut[23:20]));  // open: dp
  Hex_Digit_Display hex_digit_display_4 (.value(SyscallOut[19:16]));  // open: dp
  Hex_Digit_Display hex_digit_display_5 (.value(SyscallOut[15:12]));  // open: dp
  Hex_Digit_Display hex_digit_display_6 (.value(SyscallOut[11:8]));  // open: dp
  Hex_Digit_Display hex_digit_display_7 (.value(SyscallOut[7:4]));  // open: dp
  Hex_Digit_Display hex_digit_display_8 (.value(SyscallOut[3:0]));  // open: dp
  ROM #(.addrWidth(10), .dataWidth(32)) rom_1 (.addr(divider_1_out_2), .data(rom_1_data));  // open: sel
  or or_1 (or_1_out, RST, Fail);
  IF_ID if_id_1 (
    .in_1(npc_1_pc4), .in_2(rom_1_data), .\传输状态In (lock_IF_ID), .CLK(CLK), .out_6(if_id_1_out_6),
    .out_7(if_id_1_out_7), .\同步清零 (or_1_out));  // open: 传输状态Out
  Controller controller_1 (
    .op(decoder_1_op), .funct(decoder_1_funct), .pc_control(controller_1_pc_control), .clk(CLK), .rst(RST),
    .\有条件Cnt (\有条件分支指令数 ), .\无条件Cnt (\无条件分支指令数 ), .ex(controller_1_ex), .mem(controller_1_mem),
    .WB(controller_1_wb), .instruction(controller_1_instruction), .mix(decoder_1_mix),
    .will_r(controller_1_will_r), .ra(controller_1_ra), .rb(controller_1_rb));
  // Probe on \总周期数 
  // Probe on \无条件分支指令数 
  // Probe on \有条件分支指令数 
  // Probe on \有条件分支成功跳转 
  Multiplexer #(.select(2), .width(32), .disabled(0), .enable("false")) multiplexer_1 (
    .in0(mem_wb_1_out_13), .in1(mem_wb_1_out_9), .in2(mem_wb_1_out_12), .out(multiplexer_1_out),
    .sel(registerfile_1_p4[6:5]));  // open: in3
  Decoder decoder_1 (
    .shamt(decoder_1_shamt), .op(decoder_1_op), .label(decoder_1_label), .instruction(if_id_1_out_7),
    .funct(decoder_1_funct), .IMM(decoder_1_imm), .MIX(decoder_1_mix));
  Bubble bubble_1 (
    .rst_ID_EX(rst_ID_EX), .lock_PC(lock_PC), .will_r(controller_1_will_r), .rst(RST),
    .WB_EX(id_ex_1_out_17), .WB_MEM(ex_mem_1_out_12), .lock_IF_ID(lock_IF_ID), .ctl(CTL));
  // RegisterFile registerfile_1: pin names not known; wires that end beside it: multiplexer_1_out, CLK, registerfile_1_p4[7], registerfile_1_p4[4:0], controller_1_ra, controller_1_rb, registerfile_1_p7, registerfile_1_p8
  Extender extender_1 (
    .in_1(decoder_1_shamt), .out_3(extender_1_out_3), .out_4(extender_1_out_4), .in_2(decoder_1_imm));
  ID_EX id_ex_1 (
    .WB(controller_1_wb), .MEM(controller_1_mem), .EX(controller_1_ex), .A(registerfile_1_p7),
    .B(registerfile_1_p8), .shamt(extender_1_out_3), .IMM(extender_1_out_4), .\传输状态In (CTL), .CLK(CLK),
    .out_17(id_ex_1_out_17), .out_18(id_ex_1_out_18), .out_19(id_ex_1_out_19), .out_20(id_ex_1_out_20),
    .out_21(id_ex_1_out_21), .out_22(id_ex_1_out_22), .out_23(id_ex_1_out_23), .\同步清零 (or_2_out),
    .PC4(if_id_1_out_6), .out_15(id_ex_1_out_15), .instruction(controller_1_instruction),
    .out_16(id_ex_1_out_16), .PC_control(controller_1_pc_control), .out_24(id_ex_1_out_24),
    .Label(decoder_1_label), .out_25(id_ex_1_out_25));  // open: 传输状态Out
  or or_2 (or_2_out, Fail, rst_ID_EX);
  Syscall1 syscall1_1 (.en(id_ex_1_out_19[6]), .cnt(SyscallOut), .clk(CLK), .rst(RST), .a0(id_ex_1_out_21));
  Multiplexer #(.width(32), .disabled(0), .enable("false")) multiplexer_2 (
    .in0(id_ex_1_out_20), .in1(id_ex_1_out_22), .out(multiplexer_2_out), .sel(id_ex_1_out_19[0]));
  ALU alu_1 (.AluOP(id_ex_1_out_19[5:2]), .X(multiplexer_2_out), .Result(alu_1_result), .Y(multiplexer_3_out));
  Multiplexer #(.width(32), .disabled(0), .enable("false")) multiplexer_3 (
    .in0(id_ex_1_out_21), .in1(id_ex_1_out_23), .out(multiplexer_3_out), .sel(id_ex_1_out_19[1]));
  EX_MEM ex_mem_1 (
    .WB(id_ex_1_out_17), .MEM(id_ex_1_out_18), .ALUout(alu_1_result), .B(id_ex_1_out_21), .\传输状态In (CTL),
    .CLK(CLK), .out_12(ex_mem_1_out_12), .out_13(ex_mem_1_out_13), .out_14(ex_mem_1_out_14),
    .out_15(ex_mem_1_out_15), .\同步清零 (RST), .PC4(id_ex_1_out_15), .out_10(ex_mem_1_out_10),
    .instruction(id_ex_1_out_16), .out_11(ex_mem_1_out_11));  // open: 传输状态Out
  Divider1 divider1_1 (.in_1(ex_mem_1_out_14), .out_2(divider1_1_out_2));
  // MIPS_RAM mips_ram_1: pin names not known; wires that end beside it: divider1_1_out_2, ex_mem_1_out_15, ex_mem_1_out_13[1], ex_mem_1_out_13[5:2], CLK, ex_mem_1_out_13[0], RST, mips_ram_1_p8
  MEM_WB mem_wb_1 (
    .WB(ex_mem_1_out_12), .\传输状态In (CTL), .CLK(CLK), .out_11(registerfile_1_p4), .\同步清零 (RST),
    .ALUout(ex_mem_1_out_14), .out_13(mem_wb_1_out_13), .Data(mips_ram_1_p8), .out_12(mem_wb_1_out_12),
    .PC4(ex_mem_1_out_10), .out_9(mem_wb_1_out_9), .instruction(ex_mem_1_out_11), .out_10(mem_wb_1_out_10));  // open: 传输状态Out
  Cmp syscall (.lhs(mem_wb_1_out_10), .rhs(5'b11011), .res_n(syscall_res_n));  // open: res

  // Notes on the sheet:
  //   数码管输出应该用寄存器锁存，否则显示数据只能一闪而过
  //   可以通过项目增加Logisim库的方式将前几次实验完成的电路作为子电路引入到本电路中使用
  //   数码管输出
  //   contents of rom_1 (hex, n*v repeats v):
  //   20110001 8000c05 20110001 20120002 20130003 8000c09 20110001 20120002 20130003 8000c0d 20110001
  //   20120002 20130003 8000c11 20110001 20120002 20130003 c000cb8 20100001 20110001 118fc0 112020
  //   20020022 c 118882 12200001 8000c15 112020 20020022 c 20110001 118880 112020 20020022 c 12200001
  //   8000c1f 20110001 118fc0 112020 20020022 c 1188c3 112020 20020022 c 118903 112020 20020022 c 118903
  //   112020 20020022 c 118903 112020 20020022 c 118903 112020 20020022 c 118903 112020 20020022 c 118903
  //   112020 20020022 c 118903 112020 20020022 c 20100001 109fc0 139fc3 8021 2012000c 24160003 26100001
  //   3210000f 20080008 20090001 139900 2709825 132020 20020022 c 1094022 1500fff9 22100001 2018000f
  //   2188024 108700 20080008 20090001 139902 2709825 132021 20020022 c 1094022 1500fff9 108702 2c9b022
  //   12c00001 8000c50 4020 1084027 84400 3508ffff 82021 20020022 c 2010ffff 20110000 ae300000 22100001
  //   22310004 ae300000 22100001 22310004 ae300000 22100001 22310004 ae300000 22100001 22310004 ae300000
  //   22100001 22310004 ae300000 22100001 22310004 ae300000 22100001 22310004 ae300000 22100001 22310004
  //   ae300000 22100001 22310004 ae300000 22100001 22310004 ae300000 22100001 22310004 ae300000 22100001
  //   22310004 ae300000 22100001 22310004 ae300000 22100001 22310004 ae300000 22100001 22310004 ae300000
  //   22100001 22310004 22100001 8020 2011003c 8e130000 8e340000 274402a 11000002 ae330000 ae140000
  //   2231fffc 1611fff8 102020 20020022 c 22100004 2011003c 1611fff2 2002000a c 20100000 22100001 102020
  //   20020022 c 22100002 102020 20020022 c 22100003 102020 20020022 c 22100004 102020 20020022 c 22100005
  //   102020 20020022 c 22100006 102020 20020022 c 22100007 102020 20020022 c 22100008 102020 20020022
  //   20020022 c 3e00008
  //   总复位信号应将除ROM以外所有存储组件全部清零
  //   alu
  //   pc4
  //   load
endmodule

module Controller (
  input  [5:0] op,
  input  [5:0] funct,
  input  clk,
  input  rst,
  input  [14:0] mix,
  output [2:0] pc_control,
  output [15:0] \有条件Cnt ,
  output [4:0] instruction,
  output [4:0] rb,
  output [4:0] ra,
  output [15:0] \无条件Cnt ,
  output [6:0] ex,
  output [5:0] mem,
  output [7:0] WB,
  output [11:0] will_r
);

  wire add, addi, addiu, adds, addu, \and , andi, ands, beq, bltz, bne, cmps, comparator_1_eq,
       comparator_16_eq, comparator_17_eq, comparator_18_eq, comparator_19_eq, comparator_20_eq,
       comparator_21_eq, comparator_22_eq, comparator_23_eq, comparator_24_eq, comparator_25_eq,
       comparator_26_eq, comparator_27_eq, comparator_28_eq, comparator_29_eq, j, jal, jr, js, \nor , \or ,
       or_2_out, or_10_out, or_12_out, or_13_out, ori, ors, Ra_t, rlshifters, sb, sll, slt, slti, sltu, sra,
       srl, srlv, sub, sw, tmpR, xori;
  wire [1:0] Rw;

  Comparator #(.width(6)) comparator_1 (.a(op), .b({6{1'b0}}), .eq(comparator_1_eq));  // open: gt, lt
  Comparator #(.width(6)) comparator_2 (.a(op), .b(6'b001000), .eq(addi));  // open: gt, lt
  Comparator #(.width(6)) comparator_3 (.a(op), .b(6'b001001), .eq(addiu));  // open: gt, lt
  Comparator #(.width(6)) comparator_4 (.a(op), .b(6'b001100), .eq(andi));  // open: gt, lt
  Comparator #(.width(6)) comparator_5 (.a(op), .b(6'b001101), .eq(ori));  // open: gt, lt
  Comparator #(.width(6)) comparator_6 (.a(op), .b(6'b001110), .eq(xori));  // open: gt, lt
  Comparator #(.width(6)) comparator_7 (.a(op), .b(6'b001010), .eq(slti));  // open: gt, lt
  Comparator #(.width(6)) comparator_8 (.a(op), .b(6'b100011), .eq(mem[0]));  // open: gt, lt
  Comparator #(.width(6)) comparator_9 (.a(op), .b(6'b101011), .eq(sw));  // open: gt, lt
  Comparator #(.width(6)) comparator_10 (.a(op), .b(6'b101000), .eq(sb));  // open: gt, lt
  Comparator #(.width(6)) comparator_11 (.a(op), .b(6'b000100), .eq(beq));  // open: gt, lt
  Comparator #(.width(6)) comparator_12 (.a(op), .b(6'b000101), .eq(bne));  // open: gt, lt
  Comparator #(.width(6)) comparator_13 (.a(op), .b(6'b000001), .eq(bltz));  // open: gt, lt
  Comparator #(.width(6)) comparator_14 (.a(op), .b(6'b000010), .eq(j));  // open: gt, lt
  Comparator #(.width(6)) comparator_15 (.a(op), .b(6'b000011), .eq(jal));  // open: gt, lt
  Comparator #(.width(6)) comparator_16 (.a(funct), .b(6'b100000), .eq(comparator_16_eq));  // open: gt, lt
  Comparator #(.width(6)) comparator_17 (.a(funct), .b(6'b100001), .eq(comparator_17_eq));  // open: gt, lt
  Comparator #(.width(6)) comparator_18 (.a(funct), .b(6'b100100), .eq(comparator_18_eq));  // open: gt, lt
  Comparator #(.width(6)) comparator_19 (.a(funct), .b(6'b100010), .eq(comparator_19_eq));  // open: gt, lt
  Comparator #(.width(6)) comparator_20 (.a(funct), .b(6'b100101), .eq(comparator_20_eq));  // open: gt, lt
  Comparator #(.width(6)) comparator_21 (.a(funct), .b(6'b100111), .eq(comparator_21_eq));  // open: gt, lt
  Comparator #(.width(6)) comparator_22 (.a(funct), .b(6'b000110), .eq(comparator_22_eq));  // open: gt, lt
  Comparator #(.width(6)) comparator_23 (.a(funct), .b(6'b101010), .eq(comparator_23_eq));  // open: gt, lt
  Comparator #(.width(6)) comparator_24 (.a(funct), .b(6'b101011), .eq(comparator_24_eq));  // open: gt, lt
  Comparator #(.width(6)) comparator_25 (.a(funct), .b({6{1'b0}}), .eq(comparator_25_eq));  // open: gt, lt
  Comparator #(.width(6)) comparator_26 (.a(funct), .b(6'b000011), .eq(comparator_26_eq));  // open: gt, lt
  Comparator #(.width(6)) comparator_27 (.a(funct), .b(6'b000010), .eq(comparator_27_eq));  // open: gt, lt
  Comparator #(.width(6)) comparator_28 (.a(funct), .b(6'b001000), .eq(comparator_28_eq));  // open: gt, lt
  Comparator #(.width(6)) comparator_29 (.a(funct), .b(6'b001100), .eq(comparator_29_eq));  // open: gt, lt
  and and_1 (add, comparator_1_eq, comparator_16_eq);
  and and_2 (addu, comparator_1_eq, comparator_17_eq);
  and and_3 (\and , comparator_1_eq, comparator_18_eq);
  and and_4 (sub, comparator_1_eq, comparator_19_eq);
  and and_5 (\or , comparator_1_eq, comparator_20_eq);
  and and_6 (\nor , comparator_1_eq, comparator_21_eq);
  and and_7 (srlv, comparator_1_eq, comparator_22_eq);
  and and_8 (slt, comparator_1_eq, comparator_23_eq);
  and and_9 (sltu, comparator_1_eq, comparator_24_eq);
  and and_10 (sll, comparator_1_eq, comparator_25_eq);
  and and_11 (sra, comparator_1_eq, comparator_26_eq);
  and and_12 (srl, comparator_1_eq, comparator_27_eq);
  and and_13 (jr, comparator_1_eq, comparator_28_eq);
  and and_14 (ex[6], comparator_1_eq, comparator_29_eq);
  Priority_Encoder #(.select(5)) priority_encoder_1 (
    .in0(addi), .in1(addiu), .in2(andi), .in3(ori), .in4(xori), .in5(slti), .in6(mem[0]), .in7(sw), .in8(sb),
    .in9(beq), .in10(bne), .in11(bltz), .in12(j), .in13(jal), .in14(add), .in15(addu), .in16(\and ),
    .in17(sub), .in18(\or ), .in19(\nor ), .in20(srlv), .in21(slt), .in22(sltu), .in23(sll), .in24(sra),
    .in25(srl), .in26(jr), .in27(ex[6]), .in28(1'b0), .in29(1'b0), .in30(1'b0), .in31(1'b0), .out(instruction));  // open: gs, en_out, en_in
  or or_1 (ex[0], sll, sra, srl);
  or or_2 (or_2_out, addi, addiu, andi, ori, xori, slti, mem[0], sw, sb);
  or or_3 (cmps, slti, bltz, slt);
  or or_4 (ors, \or , ori);
  or or_5 (ands, \and , andi);
  or or_6 (rlshifters, srlv, srl);
  Priority_Encoder #(.select(1)) priority_encoder_2 (
    .in0(1'b1), .in1(or_2_out), .out(ex[1]));  // open: gs, en_out, en_in
  or or_7 (adds, mem[0], add, addi, sb, addu, addiu, sw);
  Priority_Encoder #(.select(4)) priority_encoder_3 (
    .in0(1'b1), .in1(sra), .in2(rlshifters), .in3(1'b0), .in4(1'b0), .in5(adds), .in6(sub), .in7(ands),
    .in8(ors), .in9(xori), .in10(\nor ), .in11(cmps), .in12(sltu), .in13(1'b0), .in14(1'b0), .in15(1'b0),
    .out(ex[5:2]));  // open: gs, en_out, en_in
  Multiplexer #(.select(2), .width(5), .disabled(0), .enable("false")) multiplexer_1 (
    .in0(mix[4:0]), .in1(mix[9:5]), .in2({5{1'b1}}), .out(WB[4:0]), .sel(Rw));  // open: in3
  Multiplexer #(.width(5), .disabled(0), .enable("false")) multiplexer_2 (
    .in0(mix[9:5]), .in1(5'b00100), .out(rb), .sel(Ra_t));
  Multiplexer #(.width(5), .disabled(0), .enable("false")) multiplexer_3 (
    .in0(mix[14:10]), .in1(5'b00010), .out(ra), .sel(Ra_t));
  not not_1 (mem[5], sb);
  or or_8 (mem[1], sw, sb);
  Priority_Encoder #(.select(1)) priority_encoder_4 (.in0(1'b1), .in1(ex[6]), .out(Ra_t));  // open: gs, en_out, en_in
  or or_9 (tmpR, addi, addiu, andi, ori, xori, slti, mem[0]);
  Priority_Encoder #(.select(2)) priority_encoder_5 (
    .in0(1'b1), .in1(jal), .in2(mem[0]), .in3(1'b0), .out(WB[6:5]));  // open: gs, en_out, en_in
  nor nor_1 (WB[7], sw, sb, beq, bne, bltz, j, jr, ex[6]);
  Priority_Encoder #(.select(2)) priority_encoder_6 (
    .in0(1'b1), .in1(tmpR), .in2(jal), .in3(1'b0), .out(Rw));  // open: gs, en_out, en_in
  or or_10 (or_10_out, jr, tmpR);
  Priority_Encoder #(.select(2)) priority_encoder_7 (
    .in0(1'b1), .in1(or_10_out), .in2(js), .in3(1'b0), .out(will_r[1:0]));  // open: gs, en_out, en_in
  or or_11 (js, j, jal);
  Priority_Encoder priority_encoder_8 (
    .in0(1'b1), .in1(beq), .in2(bne), .in3(bltz), .in4(js), .in5(jr), .in6(1'b0), .in7(1'b0), .out(pc_control));  // open: en_in, gs, en_out
  Counter #(.width(16), .max('hffff)) counter_1 (
    .count(or_12_out), .Q(\有条件Cnt ), .clk(clk), .clr(rst));  // open: load, D, carry
  or or_12 (or_12_out, bltz, bne, beq);
  Counter #(.width(16), .max('hffff)) counter_2 (
    .count(or_13_out), .Q(\无条件Cnt ), .clk(clk), .clr(rst));  // open: load, D, carry
  or or_13 (or_13_out, j, jal, jr);

  assign mem[4:2] = {{2{mem[5]}}, 1'b1};
  assign will_r[11:2] = {rb, ra};

  // Other names for the same wires on the sheet: CPC[2:0] = pc_control; CA = ex[0]; CB = ex[1]; ALUop[3:0] = ex[5:2];
  //   SysC1 = ex[6]; syscall = ex[6]; ld = mem[0]; lw = mem[0]; str = mem[1]; Sel[3:1] = {3{mem[5]}};
  //   rt[4:0] = mix[9:5]; rs[4:0] = mix[14:10]; Rb_t = Ra_t; RWR[4:0] = WB[4:0]; Din[1:0] = WB[6:5]; We = WB[7];
  //   will_r_t[1:0] = will_r[1:0]; 无条件[15:0] = \无条件Cnt ; 有条件[15:0] = \有条件Cnt 
endmodule

module NPC (
  input  [31:0] IMM,
  input  [31:0] PC_input,
  input  [31:0] oldPC,
  input  syscall,
  input  [31:0] RF1,
  input  [2:0] pc_control,
  input  [31:0] ALUout,
  input  clk,
  input  rst,
  input  [25:0] label,
  input  [31:0] RF2,
  output [31:0] new_PC,
  output en,
  output [31:0] PC4,
  output fail,
  output [15:0] \成功Cnt 
);

  wire and_2_out, and_3_out, and_4_out, comparator_1_eq, comparator_2_eq, comparator_3_eq, comparator_4_eq,
       comparator_5_eq, comparator_6_eq, decoder_1_out1, decoder_1_out2, decoder_1_out3, decoder_1_out4,
       decoder_1_out5, not_1_out, not_2_out, not_3_out, or_3_out, or_4_out, or_5_out;
  wire [31:0] and_1_out, bit_extender_1_out, Cbeq, Cbltz, Cbne, PC4offset, PCLabel, shifter_1_out;

  Shifter #(.width(32)) shifter_1 (.in(IMM), .\dist (5'b00010), .out(shifter_1_out));
  Adder #(.width(32)) adder_1 (.a(PC_input), .b(32'h4), .out(PC4));  // open: cin, cout
  Comparator #(.width(32)) comparator_1 (.a(RF1), .b(32'h22), .eq(comparator_1_eq));  // open: gt, lt
  assign and_1_out = PC_input & 32'hf0000000;  // AND_Gate and_1, 32 bits wide
  assign bit_extender_1_out = {{4{1'b0}}, {label, 2'b00}};  // Bit_Extender bit_extender_1
  Adder #(.width(32)) adder_2 (.a(shifter_1_out), .b(oldPC), .out(PC4offset));  // open: cin, cout
  assign PCLabel = and_1_out | bit_extender_1_out;  // OR_Gate or_1, 32 bits wide
  or or_2 (en, comparator_1_eq, syscall);
  Comparator #(.width(32)) comparator_2 (.a(RF1), .b(RF2), .eq(comparator_2_eq));  // open: gt, lt
  Multiplexer #(.width(32), .disabled(0), .enable("false")) multiplexer_1 (
    .in0(PC4), .in1(PC4offset), .out(Cbeq), .sel(comparator_2_eq));
  Multiplexer #(.width(32), .disabled(0), .enable("false")) multiplexer_2 (
    .in0(PC4offset), .in1(PC4), .out(Cbne), .sel(comparator_2_eq));
  Comparator #(.width(3)) comparator_3 (.a(pc_control), .b(3'b001), .eq(comparator_3_eq));  // open: gt, lt
  Comparator #(.width(3)) comparator_4 (.a(pc_control), .b(3'b010), .eq(comparator_4_eq));  // open: gt, lt
  not not_1 (not_1_out, comparator_2_eq);
  Comparator #(.width(3)) comparator_5 (.a(pc_control), .b(3'b011), .eq(comparator_5_eq));  // open: gt, lt
  Comparator #(.width(32)) comparator_6 (.a(ALUout), .b(32'h1), .eq(comparator_6_eq));  // open: gt, lt
  Multiplexer #(.width(32), .disabled(0), .enable("false")) multiplexer_3 (
    .in0(PC4), .in1(PC4offset), .out(Cbltz), .sel(comparator_6_eq));
  not not_2 (not_2_out, comparator_2_eq);
  not not_3 (not_3_out, or_4_out);
  and and_2 (and_2_out, comparator_3_eq, comparator_2_eq);
  and and_3 (and_3_out, comparator_4_eq, not_1_out);
  and and_4 (and_4_out, comparator_5_eq, comparator_6_eq);
  Decoder_part #(.select(3), .enable("false")) decoder_1 (
    .out1(decoder_1_out1), .out2(decoder_1_out2), .out3(decoder_1_out3), .out4(decoder_1_out4),
    .out5(decoder_1_out5), .sel(pc_control));  // open: out0, out6, out7
  or or_3 (or_3_out, comparator_2_eq, not_2_out, not_3_out);
  Counter #(.width(16), .max('hffff)) counter_1 (
    .count(or_4_out), .Q(\成功Cnt ), .clk(clk), .clr(rst));  // open: load, D, carry
  or or_4 (or_4_out, and_2_out, and_3_out, and_4_out);
  or or_5 (or_5_out, decoder_1_out1, decoder_1_out2, decoder_1_out3, decoder_1_out4, decoder_1_out5);
  and and_5 (fail, or_5_out, or_3_out);
  Multiplexer #(.select(3), .width(32), .disabled(0), .enable("false")) multiplexer_4 (
    .in0(PC4), .in1(Cbeq), .in2(Cbne), .in3(Cbltz), .in4(PCLabel), .in5(RF1), .in6({32{1'b0}}),
    .in7({32{1'b0}}), .out(new_PC), .sel(pc_control));

  // Other names for the same wires on the sheet: CNPC[2:0] = pc_control; Input[31:0] = PC_input; oldPC4[31:0] = oldPC;
  //   Output[31:0] = new_PC; success[15:0] = \成功Cnt 
endmodule

module Divider (
  input  [31:0] in_1,
  output [9:0] out_2
);


  assign out_2 = in_1[11:2];

  // Other names for the same wires on the sheet: Input[31:0] = in_1; Output[9:0] = in_1[11:2]
endmodule

module Divider1 (
  input  [31:0] in_1,
  output [23:0] out_2
);


  assign out_2 = in_1[25:2];

  // Other names for the same wires on the sheet: Input[31:0] = in_1; Output[23:0] = in_1[25:2]
endmodule

module Decoder (
  input  [31:0] instruction,
  output [4:0] shamt,
  output [5:0] op,
  output [25:0] label,
  output [14:0] MIX,
  output [5:0] funct,
  output [15:0] IMM
);


  assign funct = instruction[5:0];
  assign IMM = instruction[15:0];
  assign label = instruction[25:0];
  assign MIX = instruction[25:11];
  assign op = instruction[31:26];
  assign shamt = instruction[10:6];

  // Other names for the same wires on the sheet: Input[31:0] = instruction; s[4:0] = instruction[10:6];
  //   rd[4:0] = instruction[15:11]; rt[4:0] = instruction[20:16]; rs[4:0] = instruction[25:21]
endmodule

module Extender (
  input  [4:0] in_1,
  input  [15:0] in_2,
  output [31:0] out_3,
  output [31:0] out_4
);

  assign out_3 = {{27{in_1[4]}}, in_1};  // Bit_Extender bit_extender_1
  assign out_4 = {{16{in_2[15]}}, in_2};  // Bit_Extender bit_extender_2

  // Other names for the same wires on the sheet: eIMM[31:0] = out_4; es[31:0] = out_3; IMM[15:0] = in_2;
  //   s[4:0] = in_1
endmodule

module Syscall (
  input  in_1,
  input  in_2,
  output out_3
);

  wire not_1_out;

  not not_1 (not_1_out, in_1);
  or or_1 (out_3, not_1_out, in_2);

  // Other names for the same wires on the sheet: enable = out_3; eq = in_1; syscall = in_2
endmodule

module SumPeriod (
  input  in_1,
  input  in_2,
  input  in_3,
  output [15:0] out_4
);

  wire [15:0] adder_1_out, counter_1_q;

  Counter #(.width(16), .max('hffff)) counter_1 (
    .count(in_1), .Q(counter_1_q), .clk(in_2), .clr(in_3));  // open: load, D, carry
  Adder #(.width(16)) adder_1 (.a(16'h1), .b(counter_1_q), .out(adder_1_out));  // open: cin, cout
  Multiplexer #(.width(16), .disabled(0), .enable("false")) multiplexer_1 (
    .in0(adder_1_out), .in1(counter_1_q), .out(out_4), .sel(in_1));

  // Other names for the same wires on the sheet: CLK = in_2; cnt[15:0] = out_4; enable = in_1; RST = in_3
endmodule

module Syscall1 (
  input  en,
  input  clk,
  input  rst,
  input  [31:0] a0,
  output [31:0] cnt
);

  Register #(.width(32)) register_1 (.D(a0), .en(en), .Q(cnt), .clk(clk), .clr(rst));

  // Other names for the same wires on the sheet: enable = en; Input[31:0] = a0; Output[31:0] = cnt
endmodule

module IF_ID (
  input  [31:0] in_1,
  input  [31:0] in_2,
  input  \传输状态In ,
  input  CLK,
  input  \同步清零 ,
  output [31:0] out_6,
  output [31:0] out_7,
  output \传输状态Out 
);

  wire multiplexer_3_out;
  wire [31:0] multiplexer_1_out, multiplexer_2_out;

  Multiplexer #(.width(32), .enable("false")) multiplexer_1 (
    .in0(in_1), .in1({32{1'b0}}), .out(multiplexer_1_out), .sel(\同步清零 ));
  Multiplexer #(.width(32), .enable("false")) multiplexer_2 (
    .in0(in_2), .in1({32{1'b0}}), .out(multiplexer_2_out), .sel(\同步清零 ));
  Multiplexer #(.enable("false")) multiplexer_3 (.in0(\传输状态In ), .in1(1'b0), .out(multiplexer_3_out), .sel(\同步清零 ));
  Register #(.width(32)) register_1 (.D(multiplexer_1_out), .en(\传输状态In ), .Q(out_6), .clk(CLK));  // open: clr
  Register #(.width(32)) register_2 (.D(multiplexer_2_out), .en(\传输状态In ), .Q(out_7), .clk(CLK));  // open: clr
  Register #(.width(1)) register_3 (.D(multiplexer_3_out), .en(\传输状态In ), .Q(\传输状态Out ), .clk(CLK));  // open: clr
endmodule

module ID_EX (
  input  [31:0] PC4,
  input  [4:0] instruction,
  input  [7:0] WB,
  input  [5:0] MEM,
  input  [6:0] EX,
  input  [31:0] A,
  input  [31:0] B,
  input  [31:0] shamt,
  input  [31:0] IMM,
  input  [2:0] PC_control,
  input  [25:0] Label,
  input  \传输状态In ,
  input  CLK,
  input  \同步清零 ,
  output [31:0] out_15,
  output [4:0] out_16,
  output [7:0] out_17,
  output [5:0] out_18,
  output [6:0] out_19,
  output [31:0] out_20,
  output [31:0] out_21,
  output [31:0] out_22,
  output [31:0] out_23,
  output [2:0] out_24,
  output [25:0] out_25,
  output \传输状态Out 
);

  wire multiplexer_12_out;
  wire [2:0] multiplexer_10_out;
  wire [4:0] multiplexer_2_out;
  wire [5:0] multiplexer_4_out;
  wire [6:0] multiplexer_5_out;
  wire [7:0] multiplexer_3_out;
  wire [25:0] multiplexer_11_out;
  wire [31:0] multiplexer_1_out, multiplexer_6_out, multiplexer_7_out, multiplexer_8_out, multiplexer_9_out;

  Multiplexer #(.width(32), .enable("false")) multiplexer_1 (
    .in0(PC4), .in1({32{1'b0}}), .out(multiplexer_1_out), .sel(\同步清零 ));
  Multiplexer #(.width(5), .enable("false")) multiplexer_2 (
    .in0(instruction), .in1({5{1'b0}}), .out(multiplexer_2_out), .sel(\同步清零 ));
  Multiplexer #(.width(8), .enable("false")) multiplexer_3 (
    .in0(WB), .in1({8{1'b0}}), .out(multiplexer_3_out), .sel(\同步清零 ));
  Multiplexer #(.width(6), .enable("false")) multiplexer_4 (
    .in0(MEM), .in1({6{1'b0}}), .out(multiplexer_4_out), .sel(\同步清零 ));
  Multiplexer #(.width(7), .enable("false")) multiplexer_5 (
    .in0(EX), .in1({7{1'b0}}), .out(multiplexer_5_out), .sel(\同步清零 ));
  Multiplexer #(.width(32), .enable("false")) multiplexer_6 (
    .in0(A), .in1({32{1'b0}}), .out(multiplexer_6_out), .sel(\同步清零 ));
  Multiplexer #(.width(32), .enable("false")) multiplexer_7 (
    .in0(B), .in1({32{1'b0}}), .out(multiplexer_7_out), .sel(\同步清零 ));
  Multiplexer #(.width(32), .enable("false")) multiplexer_8 (
    .in0(shamt), .in1({32{1'b0}}), .out(multiplexer_8_out), .sel(\同步清零 ));
  Multiplexer #(.width(32), .enable("false")) multiplexer_9 (
    .in0(IMM), .in1({32{1'b0}}), .out(multiplexer_9_out), .sel(\同步清零 ));
  Multiplexer #(.width(3), .enable("false")) multiplexer_10 (
    .in0(PC_control), .in1(3'b000), .out(multiplexer_10_out), .sel(\同步清零 ));
  Multiplexer #(.width(26), .enable("false")) multiplexer_11 (
    .in0(Label), .in1({26{1'b0}}), .out(multiplexer_11_out), .sel(\同步清零 ));
  Multiplexer #(.enable("false")) multiplexer_12 (.in0(\传输状态In ), .in1(1'b0), .out(multiplexer_12_out), .sel(\同步清零 ));
  Register #(.width(32)) register_1 (.D(multiplexer_1_out), .en(\传输状态In ), .Q(out_15), .clk(CLK));  // open: clr
  Register #(.width(5)) register_2 (.D(multiplexer_2_out), .en(\传输状态In ), .Q(out_16), .clk(CLK));  // open: clr
  Register register_3 (.D(multiplexer_3_out), .en(\传输状态In ), .Q(out_17), .clk(CLK));  // open: clr
  Register #(.width(6)) register_4 (.D(multiplexer_4_out), .en(\传输状态In ), .Q(out_18), .clk(CLK));  // open: clr
  Register #(.width(7)) register_5 (.D(multiplexer_5_out), .en(\传输状态In ), .Q(out_19), .clk(CLK));  // open: clr
  Register #(.width(32)) register_6 (.D(multiplexer_6_out), .en(\传输状态In ), .Q(out_20), .clk(CLK));  // open: clr
  Register #(.width(32)) register_7 (.D(multiplexer_7_out), .en(\传输状态In ), .Q(out_21), .clk(CLK));  // open: clr
  Register #(.width(32)) register_8 (.D(multiplexer_8_out), .en(\传输状态In ), .Q(out_22), .clk(CLK));  // open: clr
  Register #(.width(32)) register_9 (.D(multiplexer_9_out), .en(\传输状态In ), .Q(out_23), .clk(CLK));  // open: clr
  Register #(.width(3)) register_10 (.D(multiplexer_10_out), .en(\传输状态In ), .Q(out_24), .clk(CLK));  // open: clr
  Register #(.width(26)) register_11 (.D(multiplexer_11_out), .en(\传输状态In ), .Q(out_25), .clk(CLK));  // open: clr
  Register #(.width(1)) register_12 (.D(multiplexer_12_out), .en(\传输状态In ), .Q(\传输状态Out ), .clk(CLK));  // open: clr
endmodule

module EX_MEM (
  input  [31:0] PC4,
  input  [4:0] instruction,
  input  [7:0] WB,
  input  [5:0] MEM,
  input  [31:0] ALUout,
  input  [31:0] B,
  input  \传输状态In ,
  input  CLK,
  input  \同步清零 ,
  output [31:0] out_10,
  output [4:0] out_11,
  output [7:0] out_12,
  output [5:0] out_13,
  output [31:0] out_14,
  output [31:0] out_15,
  output \传输状态Out 
);

  wire multiplexer_7_out;
  wire [4:0] multiplexer_2_out;
  wire [5:0] multiplexer_4_out;
  wire [7:0] multiplexer_3_out;
  wire [31:0] multiplexer_1_out, multiplexer_5_out, multiplexer_6_out;

  Multiplexer #(.width(32), .enable("false")) multiplexer_1 (
    .in0(PC4), .in1({32{1'b0}}), .out(multiplexer_1_out), .sel(\同步清零 ));
  Multiplexer #(.width(5), .enable("false")) multiplexer_2 (
    .in0(instruction), .in1({5{1'b0}}), .out(multiplexer_2_out), .sel(\同步清零 ));
  Multiplexer #(.width(8), .enable("false")) multiplexer_3 (
    .in0(WB), .in1({8{1'b0}}), .out(multiplexer_3_out), .sel(\同步清零 ));
  Multiplexer #(.width(6), .enable("false")) multiplexer_4 (
    .in0(MEM), .in1({6{1'b0}}), .out(multiplexer_4_out), .sel(\同步清零 ));
  Multiplexer #(.width(32), .enable("false")) multiplexer_5 (
    .in0(ALUout), .in1({32{1'b0}}), .out(multiplexer_5_out), .sel(\同步清零 ));
  Multiplexer #(.width(32), .enable("false")) multiplexer_6 (
    .in0(B), .in1({32{1'b0}}), .out(multiplexer_6_out), .sel(\同步清零 ));
  Multiplexer #(.enable("false")) multiplexer_7 (.in0(\传输状态In ), .in1(1'b0), .out(multiplexer_7_out), .sel(\同步清零 ));
  Register #(.width(32)) register_1 (.D(multiplexer_1_out), .en(\传输状态In ), .Q(out_10), .clk(CLK));  // open: clr
  Register #(.width(5)) register_2 (.D(multiplexer_2_out), .en(\传输状态In ), .Q(out_11), .clk(CLK));  // open: clr
  Register register_3 (.D(multiplexer_3_out), .en(\传输状态In ), .Q(out_12), .clk(CLK));  // open: clr
  Register #(.width(6)) register_4 (.D(multiplexer_4_out), .en(\传输状态In ), .Q(out_13), .clk(CLK));  // open: clr
  Register #(.width(32)) register_5 (.D(multiplexer_5_out), .en(\传输状态In ), .Q(out_14), .clk(CLK));  // open: clr
  Register #(.width(32)) register_6 (.D(multiplexer_6_out), .en(\传输状态In ), .Q(out_15), .clk(CLK));  // open: clr
  Register #(.width(1)) register_7 (.D(multiplexer_7_out), .en(\传输状态In ), .Q(\传输状态Out ), .clk(CLK));  // open: clr
endmodule

module MEM_WB (
  input  [31:0] PC4,
  input  [4:0] instruction,
  input  [7:0] WB,
  input  [31:0] Data,
  input  [31:0] ALUout,
  input  \传输状态In ,
  input  CLK,
  input  \同步清零 ,
  output [31:0] out_9,
  output [4:0] out_10,
  output [7:0] out_11,
  output [31:0] out_12,
  output [31:0] out_13,
  output \传输状态Out 
);

  wire multiplexer_6_out;
  wire [4:0] multiplexer_2_out;
  wire [7:0] multiplexer_3_out;
  wire [31:0] multiplexer_1_out, multiplexer_4_out, multiplexer_5_out;

  Multiplexer #(.width(32), .enable("false")) multiplexer_1 (
    .in0(PC4), .in1({32{1'b0}}), .out(multiplexer_1_out), .sel(\同步清零 ));
  Multiplexer #(.width(5), .enable("false")) multiplexer_2 (
    .in0(instruction), .in1({5{1'b0}}), .out(multiplexer_2_out), .sel(\同步清零 ));
  Multiplexer #(.width(8), .enable("false")) multiplexer_3 (
    .in0(WB), .in1({8{1'b0}}), .out(multiplexer_3_out), .sel(\同步清零 ));
  Multiplexer #(.width(32), .enable("false")) multiplexer_4 (
    .in0(Data), .in1({32{1'b0}}), .out(multiplexer_4_out), .sel(\同步清零 ));
  Multiplexer #(.width(32), .enable("false")) multiplexer_5 (
    .in0(ALUout), .in1({32{1'b0}}), .out(multiplexer_5_out), .sel(\同步清零 ));
  Multiplexer #(.enable("false")) multiplexer_6 (.in0(\传输状态In ), .in1(1'b0), .out(multiplexer_6_out), .sel(\同步清零 ));
  Register #(.width(32)) register_1 (.D(multiplexer_1_out), .en(\传输状态In ), .Q(out_9), .clk(CLK));  // open: clr
  Register #(.width(5)) register_2 (.D(multiplexer_2_out), .en(\传输状态In ), .Q(out_10), .clk(CLK));  // open: clr
  Register register_3 (.D(multiplexer_3_out), .en(\传输状态In ), .Q(out_11), .clk(CLK));  // open: clr
  Register #(.width(32)) register_4 (.D(multiplexer_4_out), .en(\传输状态In ), .Q(out_12), .clk(CLK));  // open: clr
  Register #(.width(32)) register_5 (.D(multiplexer_5_out), .en(\传输状态In ), .Q(out_13), .clk(CLK));  // open: clr
  Register #(.width(1)) register_6 (.D(multiplexer_6_out), .en(\传输状态In ), .Q(\传输状态Out ), .clk(CLK));  // open: clr
endmodule

module Cmp (
  input  [4:0] lhs,
  input  [4:0] rhs,
  output res,
  output res_n
);

  Comparator #(.width(5), .mode("unsigned")) comparator_1 (.a(lhs), .b(rhs), .eq(res));  // open: gt, lt
  not not_1 (res_n, res);
endmodule

module Bubble (
  input  [11:0] will_r,
  input  rst,
  input  [7:0] WB_EX,
  input  [7:0] WB_MEM,
  input  ctl,
  output rst_ID_EX,
  output lock_PC,
  output lock_IF_ID
);

  wire and_1_out, and_2_out, and_3_out, and_4_out, and_5_out, and_6_out, and_7_out, and_8_out, and_9_out,
       and_10_out, cmp_1_res_n, cmp_2_res_n, cmp_3_res, cmp_4_res, cmp_5_res, cmp_6_res, crash,
       decoder_1_out0, decoder_1_out1, decoder_1_out2, decoder_2_out0, decoder_2_out1, decoder_2_out2,
       or_1_out, or_2_out, or_3_out, or_4_out;

  Decoder_part #(.select(2), .enable("false")) decoder_1 (
    .out0(decoder_1_out0), .out1(decoder_1_out1), .out2(decoder_1_out2), .sel(will_r[1:0]));  // open: out3
  Decoder_part #(.select(2), .enable("false")) decoder_2 (
    .out0(decoder_2_out0), .out1(decoder_2_out1), .out2(decoder_2_out2), .sel(will_r[1:0]));  // open: out3
  Cmp cmp_1 (.lhs(will_r[11:7]), .rhs({5{1'b0}}), .res_n(cmp_1_res_n));  // open: res
  Cmp cmp_2 (.lhs(will_r[6:2]), .rhs({5{1'b0}}), .res_n(cmp_2_res_n));  // open: res
  Cmp cmp_3 (.lhs(will_r[11:7]), .res(cmp_3_res), .rhs(WB_EX[4:0]));  // open: res_n
  Cmp cmp_4 (.lhs(will_r[6:2]), .res(cmp_4_res), .rhs(WB_EX[4:0]));  // open: res_n
  Cmp cmp_5 (.lhs(will_r[11:7]), .res(cmp_5_res), .rhs(WB_MEM[4:0]));  // open: res_n
  Cmp cmp_6 (.lhs(will_r[6:2]), .res(cmp_6_res), .rhs(WB_MEM[4:0]));  // open: res_n
  and and_1 (and_1_out, cmp_1_res_n, cmp_3_res);
  and and_2 (and_2_out, cmp_4_res, cmp_2_res_n);
  and and_3 (and_3_out, cmp_1_res_n, cmp_5_res);
  and and_4 (and_4_out, cmp_6_res, cmp_2_res_n);
  or or_1 (or_1_out, and_1_out, and_2_out);
  and and_5 (and_5_out, decoder_1_out1, and_1_out);
  or or_2 (or_2_out, and_3_out, and_4_out);
  and and_6 (and_6_out, decoder_2_out1, and_3_out);
  and and_7 (and_7_out, or_1_out, decoder_1_out0);
  and and_8 (and_8_out, or_2_out, decoder_2_out0);
  or or_3 (or_3_out, and_7_out, and_5_out);
  and and_9 (and_9_out, or_3_out, ~decoder_1_out2);  // AND_Gate
  or or_4 (or_4_out, and_8_out, and_6_out);
  and and_10 (and_10_out, or_4_out, ~decoder_2_out2);  // AND_Gate
  or or_5 (crash, and_9_out, and_10_out);
  or or_6 (rst_ID_EX, rst, crash);
  not not_1 (lock_PC, crash);
  and and_11 (lock_IF_ID, ~crash, ctl);  // AND_Gate

  // Other names for the same wires on the sheet: RWR_EX[4:0] = WB_EX[4:0]; Din_EX[1:0] = WB_EX[6:5]; We_EX = WB_EX[7];
  //   RWR_MEM[4:0] = WB_MEM[4:0]; Din_MEM[1:0] = WB_MEM[6:5]; We_MEM = WB_MEM[7]; will_r_t[1:0] = will_r[1:0];
  //   rt[4:0] = will_r[6:2]; rs[4:0] = will_r[11:7]
endmodule
